// Logisim project LFSR.circ as structural Verilog: 1 circuit, main circuit main
module main (
  input  in_1
);

  wire clock_1_out, shift_register_1_q30, shift_register_1_q31, xor_1_out;

  Clock clock_1 (.out(clock_1_out));
  xor xor_1 (xor_1_out, shift_register_1_q31, shift_register_1_q30);
  Shift_Register #(.length(32)) shift_register_1 (
    .shift(in_1), .in(xor_1_out), .clk(clock_1_out), .q30(shift_register_1_q30), .q31(shift_register_1_q31));  // open: out, load, clr, d0, q0, d1, q1, d2, q2, d3, q3, d4, q4, d5, q5, d6, q6, d7, q7, d8, q8, d9, q9, d10, q10, d11, q11, d12, q12, d13, q13, d14, q14, d15, q15, d16, q16, d17, q17, d18, q18, d19, q19, d20, q20, d21, q21, d22, q22, d23, q23, d24, q24, d25, q25, d26, q26, d27, q27, d28, q28, d29, q29, d30, d31
endmodule
